# Fritzing sketch instrumentLayout (saved by Fritzing 0.9.3b)
perfboards: 1

parts:
  Part1 = Arduino Mega 2560 (Rev3)
  NeckPot = Basic Flex Resistor
  OctavePot = SoftPot Membrane Potentiometer - 50mm [part_number=SEN-08680]
  MainPot = SoftPot Membrane Potentiometer - 50mm [part_number=SEN-08680]
  LED1 = smd LED [color="Green (565nm)" package="1206 [SMD]"]
  LED2 = smd LED [color="Yellow (595nm)" package="1206 [SMD]"]
  LED3 = smd LED [color="Red (633nm)" package="1206 [SMD]"]
  R2 = Resistor [tolerance=±5% resistance=220 package="0402 [SMD]"]
  R3 = Resistor [tolerance=±5% resistance=220 package="0402 [SMD]"]
  R4 = Resistor [tolerance=±5% resistance=220 package="0402 [SMD]"]
  R5 = Resistor [tolerance=±5% resistance=10k package="2512 [SMD]"]
  R7 = Resistor [tolerance=±5% resistance=10k package="2512 [SMD]"]
  Part2 = Thumb Joystick
  UpButton = Round Pushbutton
  DownButton = Round Pushbutton
  ScaleButton = Round Pushbutton
  R8 = Resistor [tolerance=±5% resistance=220 package="0402 [SMD]"]
  R9 = Resistor [tolerance=±5% resistance=220 package="0402 [SMD]"]
  R10 = Resistor [tolerance=±5% resistance=220 package="0402 [SMD]"]
  LCD1 = LCD screen
  R11 = Resistor [tolerance=±5% resistance=220 package="0402 [SMD]"]
  StrumPot = Basic Force Sensing Resistor (FSR) [package=THT]
  R12 = Resistor [tolerance=±5% resistance=10k package="2512 [SMD]"]
  R13 = Resistor [tolerance=±5% resistance=10k package="2512 [SMD]"]

nets:
  N1: Part1.A8, StrumPot.pin_0, R13.Pin_1
  N2: Part1.A13, Part2.VERT
  N3: Part1.A14, Part2.HORZ
  N4: Part1.A15, NeckPot.pin_1, R12.Pin_1
  N5: Part1.A1, OctavePot.wiper, R7.Pin_0
  GND: Part1.GND, R2.Pin_0, R3.Pin_0, R4.Pin_0, Part2.GND, LCD1.VSS
  N6: Part1.D13_PWM, UpButton.leg0, R9.Pin_0
  N7: Part1.D12_PWM, DownButton.leg0, R8.Pin_0
  N8: Part1.D11_PWM, ScaleButton.leg0, R10.Pin_0
  N9: Part1.D8_PWM, Part2.SEL, R11.Pin_1
  N10: Part1.D2_PWM, LCD1.V0
  N11: Part1.D5_PWM, LED1.anode
  N12: Part1.D6_PWM, LED2.anode
  N13: Part1.D7_PWM, LED3.anode
  N14: NeckPot.Pin_2, OctavePot.leg1, MainPot.leg1, Part2.VCC, StrumPot.pin_1
  N15: OctavePot.leg2, MainPot.leg2, R5.Pin_1, R7.Pin_1, R11.Pin_0, R12.Pin_0
  N16: MainPot.wiper, R5.Pin_0
  N17: LED1.cathode, R4.Pin_1
  N18: LED2.cathode, R2.Pin_1
  N19: LED3.cathode, R3.Pin_1
  N20: ScaleButton.leg1, LCD1.VDD

custom parts:
  SoftPot Membrane Potentiometer - 50mm: These are very thin variable potentiometers. By pressing down on various parts of the strip, the resistance linearly changes from 100Ohms to 10,000Ohms allowing the user to very accurately calculate the relative position on the strip. Can be used as an accurate positional indicator for CNC head positioning, variable user input (volume level input for example), straight user input (multiple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
